# Fritzing sketch thermostat (saved by Fritzing 0.9.4)
circuit board: 5.70158cm x 5.7cm

parts:
  U2 = ESP32S-HiLetgo [part_number=ESP32S-HiLetgo]
  BM280 = AHT20 BMP280 pressure and humidity breakout
  R1 = Resistor [tolerance=±5% resistance=220 package=THT]
  LED1 = LED - 3mm [color="Red (633nm)" package="3 mm [THT]"]

nets:
  N1: U2.3.3, BM280.VDD
  N2: U2.GPIO17, R1.Pin_0
  GND: U2.GND, BM280.GND, LED1.cathode
  N3: U2.GPIO21, BM280.SDA
  N4: U2.GPIO22, BM280.SCL
  N5: R1.Pin_1, LED1.anode

custom parts:
  ESP32S-HiLetgo: HiLetgo ESP-WROOM-32 ESP32 ESP-32S Development Board 2.4GHz Dual-Mode WiFi + Bluetooth Dual Cores Microcontroller The ESP32 integrated with Antenna switches, RF Balun, power amplifiers, low-noise amplifiers, filters, and management modules, and the entire solution occupies the least area of PCB. 2.4 GHz Wi-Fi plus Bluetooth dual-mode chip, with TSMC Ultra-low power consumption 40nm technology,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
  AHT20 BMP280 pressure and humidity breakout: Cheap breakout board for the BMP280, barometric pressure sensor, and AHT20, humidity sensor
